# Fritzing sketch MovingRaspi (EBC transistor) (saved by Fritzing 0.7.11b)
breadboards: 1

parts:
  Q5 = NPN-Transistor [part_number=BCU81 package="TO92 [THT]"]
  Q8 = NPN-Transistor [part_number=BCU81 package="TO92 [THT]"]
  Q6 = NPN-Transistor [part_number=BCU81 package="TO92 [THT]"]
  Q7 = NPN-Transistor [part_number=BCU81 package="TO92 [THT]"]
  Q1 = NPN-Transistor [part_number=BCU81 package="TO92 [THT]"]
  Q2 = NPN-Transistor [part_number=BCU81 package="TO92 [THT]"]
  Q3 = NPN-Transistor [part_number=BCU81 package="TO92 [THT]"]
  Q4 = NPN-Transistor [part_number=BCU81 package="TO92 [THT]"]
  RaspberryPi1 = Raspberry Pi Model B
  D1 = Rectifier Diode [part_number=1N4001 package="300 mil [THT]"]
  D2 = Rectifier Diode [part_number=1N4001 package="300 mil [THT]"]
  D4 = Rectifier Diode [part_number=1N4001 package="300 mil [THT]"]
  D5 = Rectifier Diode [part_number=1N4001 package="300 mil [THT]"]
  D6 = Rectifier Diode [part_number=1N4001 package="300 mil [THT]"]
  D7 = Rectifier Diode [part_number=1N4001 package="300 mil [THT]"]
  D8 = Rectifier Diode [part_number=1N4001 package="300 mil [THT]"]
  R8 = Resistor [tolerance=±5% resistance=330 package=THT]
  M1 = DC Motor [part_number="Right motor"]
  M2 = DC Motor [part_number="Left motor"]
  IC2 = Microchip MCP23008 8-bit I/O expander [part_number=MCP23008 package="DIP (Dual Inline) [THT]"]
  R4 = Resistor [tolerance=±5% resistance=330 package=THT]
  R7 = Resistor [tolerance=±5% resistance=330 package=THT]
  R6 = Resistor [tolerance=±5% resistance=330 package=THT]
  R5 = Resistor [tolerance=±5% resistance=330 package=THT]
  R2 = Resistor [tolerance=±5% resistance=330 package=THT]
  R3 = Resistor [tolerance=±5% resistance=330 package=THT]
  R1 = Resistor [tolerance=±5% resistance=330 package=THT]
  D3 = Rectifier Diode [part_number=1N4001 package="300 mil [THT]"]
  C2 = Ceramic Capacitor [capacitance=100nF package="200 mil [THT, multilayer]"]
  C1 = Ceramic Capacitor [capacitance=100nF package="200 mil [THT, multilayer]"]
  VCC1 = Battery

nets:
  N1: Q5.emitter, Q8.collector, D5.anode, D8.cathode, M2.pin_1, C2.1
  N2: Q5.base, R5.Pin_1
  N3: Q5.collector, Q7.collector, Q1.collector, Q3.collector, D1.cathode, D5.cathode, D7.cathode, D3.cathode, VCC1.+
  GND: Q8.emitter, Q6.emitter, Q2.emitter, Q4.emitter, RaspberryPi1.GND, D2.anode, D4.anode, D6.anode, D8.anode, IC2.A2, IC2.A1, IC2.A0, IC2.VSS, VCC1.-
  N4: Q8.base, R8.Pin_1
  N5: Q6.base, R6.Pin_1
  N6: Q6.collector, Q7.emitter, D6.cathode, D7.anode, M2.pin_2, C2.0
  N7: Q7.base, R7.Pin_1
  N8: Q1.emitter, Q4.collector, D1.anode, D4.cathode, M1.pin_1, C1.1
  N9: Q1.base, R1.Pin_1
  N10: Q2.base, R2.Pin_1
  N11: Q2.collector, Q3.emitter, D2.cathode, M1.pin_2, D3.anode, C1.0
  N12: Q3.base, R3.Pin_1
  N13: Q4.base, R4.Pin_1
  N14: RaspberryPi1.3V3, RaspberryPi1.SDA, IC2.SDA
  5V: RaspberryPi1.5V, IC2.Reset, IC2.VDD
  N15: RaspberryPi1.SCL, IC2.SCL
  N16: R8.Pin_0, IC2.GP7
  N17: IC2.GP0, R1.Pin_0
  N18: IC2.GP1, R2.Pin_0
  N19: IC2.GP2, R3.Pin_0
  N20: IC2.GP3, R4.Pin_0
  N21: IC2.GP4, R5.Pin_0
  N22: IC2.GP5, R6.Pin_0
  N23: IC2.GP6, R7.Pin_0

custom parts:
  Raspberry Pi Model B: Raspberry Pi (Model B)
  Microchip MCP23008 8-bit I/O expander: Provides 8-bit, general purpose, parallel I/O expansion for I2C bus. Datasheet: http://ww1.microchip.com/downloads/en/devicedoc/21919e.pdf
