# Fritzing sketch Power (saved by Fritzing 0.7.10b)
stripboards: 1

parts:
  VCC1 = 4 x AAA Battery Mount
  J1 = double row male pin header, 2 pins [form="♂ (male)"]
  J2 = double row male pin header, 2 pins [form="♂ (male)"]
  CONN1 = USB connector [package=THT]
  JACK1 = 2.1mm Barrel Jack with Terminal Block

nets:
  N1: VCC1.-, J1.pin2, J2.pin2, CONN1.GND, CONN1.chassis5, CONN1.chassis6, JACK1.NEG
  N2: VCC1.+, J1.pin1, J2.pin1, CONN1.5V, JACK1.POS
