# Fritzing sketch MovingRaspi (ECB transistor) (saved by Fritzing 0.7.11b)
breadboards: 1

parts:
  RaspberryPi1 = Raspberry Pi Model B
  D1 = Rectifier Diode [part_number=1N4001 package="300 mil [THT]"]
  D2 = Rectifier Diode [part_number=1N4001 package="300 mil [THT]"]
  D4 = Rectifier Diode [part_number=1N4001 package="300 mil [THT]"]
  D5 = Rectifier Diode [part_number=1N4001 package="300 mil [THT]"]
  D6 = Rectifier Diode [part_number=1N4001 package="300 mil [THT]"]
  D7 = Rectifier Diode [part_number=1N4001 package="300 mil [THT]"]
  D8 = Rectifier Diode [part_number=1N4001 package="300 mil [THT]"]
  R8 = Resistor [tolerance=±5% resistance=330 package=THT]
  M1 = DC Motor [part_number="Right motor"]
  M2 = DC Motor [part_number="Left motor"]
  IC2 = Microchip MCP23008 8-bit I/O expander [part_number=MCP23008 package="DIP (Dual Inline) [THT]"]
  R4 = Resistor [tolerance=±5% resistance=330 package=THT]
  R7 = Resistor [tolerance=±5% resistance=330 package=THT]
  R6 = Resistor [tolerance=±5% resistance=330 package=THT]
  R5 = Resistor [tolerance=±5% resistance=330 package=THT]
  R2 = Resistor [tolerance=±5% resistance=330 package=THT]
  R3 = Resistor [tolerance=±5% resistance=330 package=THT]
  R1 = Resistor [tolerance=±5% resistance=330 package=THT]
  D3 = Rectifier Diode [part_number=1N4001 package="300 mil [THT]"]
  Q6 = NPN-Transistor [part_number=BCU81 package="TO92 [THT]"]
  Q7 = NPN-Transistor [part_number=BCU81 package="TO92 [THT]"]
  Q8 = NPN-Transistor [part_number=BCU81 package="TO92 [THT]"]
  Q5 = NPN-Transistor [part_number=BCU81 package="TO92 [THT]"]
  Q2 = NPN-Transistor [part_number=BCU81 package="TO92 [THT]"]
  Q3 = NPN-Transistor [part_number=BCU81 package="TO92 [THT]"]
  Q4 = NPN-Transistor [part_number=BCU81 package="TO92 [THT]"]
  Q1 = NPN-Transistor [part_number=BCU81 package="TO92 [THT]"]
  C2 = Ceramic Capacitor [capacitance=100nF voltage=16V package="200 mil [THT, multilayer]"]
  C1 = Ceramic Capacitor [capacitance=100nF voltage=16V package="200 mil [THT, multilayer]"]
  VCC1 = Battery

nets:
  5V: RaspberryPi1.5V, IC2.Reset, IC2.VDD
  N1: RaspberryPi1.SDA, IC2.SDA
  N2: RaspberryPi1.SCL, IC2.SCL
  GND: RaspberryPi1.GND, D2.anode, D4.anode, D6.anode, D8.anode, IC2.A2, IC2.A1, IC2.A0, IC2.VSS, Q6.E, Q8.E, Q2.E, Q4.E, VCC1.-
  N3: D1.cathode, D5.cathode, D7.cathode, D3.cathode, Q7.C, Q5.C, Q3.C, Q1.C, VCC1.+
  N4: D1.anode, D4.cathode, M1.pin_1, Q4.C, Q1.E, C1.1
  N5: D2.cathode, M1.pin_2, D3.anode, Q2.C, Q3.E, C1.0
  N6: D5.anode, D8.cathode, M2.pin_1, Q8.C, Q5.E, C2.1
  N7: D6.cathode, D7.anode, M2.pin_2, Q6.C, Q7.E, C2.0
  N8: R8.Pin_0, IC2.GP7
  N9: R8.Pin_1, Q8.B
  N10: IC2.GP0, R1.Pin_0
  N11: IC2.GP1, R2.Pin_0
  N12: IC2.GP2, R3.Pin_0
  N13: IC2.GP3, R4.Pin_0
  N14: IC2.GP4, R5.Pin_0
  N15: IC2.GP5, R6.Pin_0
  N16: IC2.GP6, R7.Pin_0
  N17: R4.Pin_1, Q4.B
  N18: R7.Pin_1, Q7.B
  N19: R6.Pin_1, Q6.B
  N20: R5.Pin_1, Q5.B
  N21: R2.Pin_1, Q2.B
  N22: R3.Pin_1, Q3.B
  N23: R1.Pin_1, Q1.B

custom parts:
  Raspberry Pi Model B: Raspberry Pi (Model B)
  Microchip MCP23008 8-bit I/O expander: Provides 8-bit, general purpose, parallel I/O expansion for I2C bus. Datasheet: http://ww1.microchip.com/downloads/en/devicedoc/21919e.pdf
