# Fritzing sketch MovingRaspi concept (saved by Fritzing 0.7.10b)
breadboards: 1

parts:
  RaspberryPi1 = Raspberry Pi Model B
  R8 = Resistor [tolerance=±5% resistance=330 package=THT]
  R4 = Resistor [tolerance=±5% resistance=330 package=THT]
  R7 = Resistor [tolerance=±5% resistance=330 package=THT]
  R6 = Resistor [tolerance=±5% resistance=330 package=THT]
  R5 = Resistor [tolerance=±5% resistance=330 package=THT]
  R2 = Resistor [tolerance=±5% resistance=330 package=THT]
  R3 = Resistor [tolerance=±5% resistance=330 package=THT]
  R1 = Resistor [tolerance=±5% resistance=330 package=THT]
  IC3 = Microchip MCP23008 8-bit I/O expander [part_number=MCP23008 package="DIP (Dual Inline) [THT]"]
  LED1 = LED - 5mm [color="Red (633nm)" package="5 mm [THT]"]
  LED2 = LED - 5mm [color="Red (633nm)" package="5 mm [THT]"]
  LED3 = LED - 5mm [color="Red (633nm)" package="5 mm [THT]"]
  LED4 = LED - 5mm [color="Red (633nm)" package="5 mm [THT]"]
  LED5 = LED - 5mm [color="Red (633nm)" package="5 mm [THT]"]
  LED6 = LED - 5mm [color="Red (633nm)" package="5 mm [THT]"]
  LED7 = LED - 5mm [color="Red (633nm)" package="5 mm [THT]"]
  LED8 = LED - 5mm [color="Red (633nm)" package="5 mm [THT]"]

nets:
  3V3: RaspberryPi1.3V3, IC3.Reset, IC3.VDD
  N1: RaspberryPi1.SDA, IC3.SDA
  N2: RaspberryPi1.SCL, IC3.SCL
  GND: RaspberryPi1.GND, IC3.A2, IC3.A1, IC3.A0, IC3.VSS, LED1.cathode, LED2.cathode, LED3.cathode, LED4.cathode, LED5.cathode, LED6.cathode, LED7.cathode, LED8.cathode
  N3: R8.Pin_0, IC3.GP7
  N4: R8.Pin_1, LED8.anode
  N5: R4.Pin_0, IC3.GP3
  N6: R4.Pin_1, LED4.anode
  N7: R7.Pin_0, IC3.GP6
  N8: R7.Pin_1, LED7.anode
  N9: R6.Pin_0, IC3.GP5
  N10: R6.Pin_1, LED6.anode
  N11: R5.Pin_0, IC3.GP4
  N12: R5.Pin_1, LED5.anode
  N13: R2.Pin_0, IC3.GP1
  N14: R2.Pin_1, LED2.anode
  N15: R3.Pin_0, IC3.GP2
  N16: R3.Pin_1, LED3.anode
  N17: R1.Pin_0, IC3.GP0
  N18: R1.Pin_1, LED1.anode

custom parts:
  Raspberry Pi Model B: Raspberry Pi (Model B)
  Microchip MCP23008 8-bit I/O expander: Provides 8-bit, general purpose, parallel I/O expansion for I2C bus. Datasheet: http://ww1.microchip.com/downloads/en/devicedoc/21919e.pdf
