# Fritzing sketch MovingRaspi (L293D) (saved by Fritzing 0.7.12b)
breadboards: 1

parts:
  RaspberryPi1 = Raspberry Pi Model B
  M1 = DC Motor [part_number="Right motor"]
  MCP23008 = Microchip MCP23008 8-bit I/O expander [part_number=MCP23008 package="DIP (Dual Inline) [THT]"]
  C1 = Ceramic Capacitor [capacitance=100nF voltage=16V package="200 mil [THT, multilayer]"]
  C2 = Ceramic Capacitor [capacitance=100nF voltage=16V package="200 mil [THT, multilayer]"]
  M2 = DC Motor [part_number="Left motor"]
  VCC1 = Battery block 9V
  L293D = L293D [package=THT]

nets:
  5V: RaspberryPi1.5V, MCP23008.Reset, MCP23008.VDD, L293D.+V
  N1: RaspberryPi1.SDA, MCP23008.SDA
  N2: RaspberryPi1.SCL, MCP23008.SCL
  GND: RaspberryPi1.GND, MCP23008.A2, MCP23008.A1, MCP23008.A0, MCP23008.VSS, VCC1.-, L293D.0V
  N3: M1.pin_1, C1.1, L293D.Out_4_(_Controlled_by_Enable_2_)
  N4: M1.pin_2, C1.0, L293D.Out_3_(_Controlled_by_Enable_2_)
  N5: MCP23008.GP0, L293D.Enable_1
  N6: MCP23008.GP1, L293D.In_1
  N7: MCP23008.GP2, L293D.In_2
  N8: MCP23008.GP4, L293D.Enable_2
  N9: MCP23008.GP5, L293D.In_4
  N10: MCP23008.GP6, L293D.In_3
  N11: C2.0, M2.pin_1, L293D.Out_2_(_Controlled_by_Enable_1_)
  N12: C2.1, M2.pin_2, L293D.Out_1_(_Controlled_by_Enable_1_)
  N13: VCC1.+, L293D.+Vmotor

custom parts:
  Raspberry Pi Model B: Raspberry Pi (Model B)
  Microchip MCP23008 8-bit I/O expander: Provides 8-bit, general purpose, parallel I/O expansion for I2C bus. Datasheet: http://ww1.microchip.com/downloads/en/devicedoc/21919e.pdf
